# Fritzing sketch sheme (saved by Fritzing 0.9.3b)

parts:
  LCD1 = LCD screen
  LCM1602_IIC2 = LCM1602 IIC [part_number="LCM1602 IIC" chip_label="LCM1602 IIC" package="DIP (Dual Inline) [THT]"]
  Part1 = Arduino Nano (Rev3.0)
  RE1 = KY-040 Rotary encoder [package=THT]
  S1 = Pushbutton [package="[THT]"]

nets:
  VSS: LCD1.VSS, LCM1602_IIC2.VSS
  VDD: LCD1.VDD, LCM1602_IIC2.VDD
  N1: LCD1.V0, LCM1602_IIC2.V0
  N2: LCD1.RS, LCM1602_IIC2.RS
  N3: LCD1.R/W, LCM1602_IIC2.RW
  N4: LCD1.E, LCM1602_IIC2.E
  N5: LCD1.DB0, LCM1602_IIC2.D0
  N6: LCD1.DB1, LCM1602_IIC2.D1
  N7: LCD1.DB2, LCM1602_IIC2.D2
  N8: LCD1.DB3, LCM1602_IIC2.D3
  N9: LCD1.DB4, LCM1602_IIC2.D4
  N10: LCD1.DB5, LCM1602_IIC2.D5
  N11: LCD1.DB6, LCM1602_IIC2.D6
  N12: LCD1.DB7, LCM1602_IIC2.D7
  N13: LCD1.LED+, LCM1602_IIC2.A
  N14: LCD1.LED-, LCM1602_IIC2.K
  GND: LCM1602_IIC2.GND, Part1.GND, RE1.GND, S1.Pin_3, S1.Pin_4
  VCC: LCM1602_IIC2.VCC, Part1.5V, RE1.Vcc
  N15: LCM1602_IIC2.SDA, Part1.A4
  N16: LCM1602_IIC2.SCL, Part1.A5
  N17: LCM1602_IIC2.LED_A, LCM1602_IIC2.LED_B
  N18: Part1.D2, RE1.CLK
  N19: Part1.D3, RE1.DT
  N20: Part1.D4, RE1.SW
  N21: Part1.D5, S1.Pin_1, S1.Pin_2

notes:
  220V AC
  Transformer
  SSR AC
  Power Suply 5VD

custom parts:
  LCM1602 IIC: I2C-Module to use a 1602 or 2004 LCD on with the wire.h libory Serial LCD Modul
  KY-040 Rotary encoder: KY-040 Rotary Encoder with switch on breakout borad from AZ Delivery
